# Fritzing sketch ArduinoScheme (saved by Fritzing 0.9.10b)
breadboards: 1

parts:
  Part1 = Arduino Uno (Rev3) - ICSP
  R1 = Resistor [tolerance=±5% power=0.25 resistance=150 package=THT]
  R2 = Resistor [tolerance=±5% power=0.25 resistance=150 package=THT]
  U1 = Sharp PC817 [package=THT]
  R3 = Resistor [tolerance=±5% power=0.25 resistance=150 package=THT]
  R4 = Resistor [tolerance=±5% power=0.25 resistance=150 package=THT]
  U2 = Sharp PC817 [package=THT]
  U3 = Sharp PC817 [package=THT]
  U4 = Sharp PC817 [package=THT]
  R5 = Resistor [tolerance=±5% power=0.25 resistance=150 package=THT]
  R6 = Resistor [tolerance=±5% power=0.25 resistance=150 package=THT]
  R7 = Resistor [tolerance=±5% power=0.25 resistance=150 package=THT]
  R8 = Resistor [tolerance=±5% power=0.25 resistance=150 package=THT]
  S1 = SWITCH-MOMENTARY-2 [package=tactile-pth-12mm]
  S2 = SWITCH-MOMENTARY-2 [package=tactile-pth-12mm]
  S3 = SWITCH-MOMENTARY-2 [package=tactile-pth-12mm]
  S4 = SWITCH-MOMENTARY-2 [package=tactile-pth-12mm]

nets:
  N1: Part1.D8, R1.Pin_0
  N2: Part1.D9_PWM, R3.Pin_0
  N3: Part1.D10_PWM/SS, R6.Pin_0
  N4: Part1.D11_PWM/MOSI, R8.Pin_0
  N5: Part1.GND, U1.Pin_2, U2.Pin_2, U3.Pin_2, U4.Pin_2
  N6: R1.Pin_1, R2.Pin_0
  N7: R2.Pin_1, U1.Pin_1
  N8: U1.Pin_4, U3.Pin_1, R7.Pin_1, S1.1
  N9: U1.Pin_3, S1.2
  N10: R3.Pin_1, R4.Pin_0
  N11: R4.Pin_1, U2.Pin_1
  N12: U2.Pin_4, S2.1
  N13: U2.Pin_3, S2.2
  N14: U3.Pin_4, S4.1
  N15: U3.Pin_3, S4.2
  N16: U4.Pin_1, R5.Pin_1
  N17: U4.Pin_4, S3.1
  N18: U4.Pin_3, S3.2
  N19: R5.Pin_0, R6.Pin_1
  N20: R7.Pin_0, R8.Pin_1

notes:
  backward
  forward
  left
  right
  PWM Legend:
  BLACK: BACKWARD
  RED: FORWARD
  ORANGE: LEFT
  YELLOW: RIGHT
